# Fritzing sketch circuit (saved by Fritzing 0.9.4)
breadboards: 1

parts:
  Raspberry_Pi1 = Raspberry Pi B+
  S1 = Square Pushbutton
  U1 = SWITCH-SPST-2 [package=switch-spst-vertical]

nets:
  N1: Raspberry_Pi1.GPIO3, S1.leg1
  N2: Raspberry_Pi1.GPIO27, U1.P
  N3: Raspberry_Pi1.GND, S1.leg0, U1.O
